// Logisim project PandesalCPU.circ as structural Verilog: 19 circuits, main circuit PandesalCPU
module PandesalCPU (
  input  Reset
);

  wire ABL_cout, and_1_out, and_2_out, and_3_out, and_4_out, and_5_out, and_6_out, clock_1_out,
       decoder_1_out0, decoder_1_out1, decoder_1_out2, decoder_1_out3, decoder_1_out4, decoder_1_out5,
       decoder_1_out6, decoder_1_out7, decoder_1_out8, decoder_1_out9, decoder_1_out10, decoder_1_out11,
       decoder_1_out12, decoder_1_out13, decoder_1_out14, decoder_1_out15, decoder_2_out0, decoder_2_out1,
       decoder_2_out2, decoder_2_out3, decoder_2_out4, decoder_2_out5, decoder_2_out6, decoder_2_out7,
       decoder_2_out8, decoder_2_out9, decoder_2_out10, decoder_2_out11, decoder_2_out12, decoder_2_out13,
       decoder_2_out14, decoder_2_out15, decoder_3_out1, decoder_3_out2, decoder_3_out3,
       demultiplexer_1_out0, demultiplexer_1_out1, demultiplexer_2_out0, demultiplexer_2_out1,
       demultiplexer_3_out0, demultiplexer_3_out1, multiplexer_1_out, multiplexer_2_out, not_1_out,
       not_2_out, not_3_out, not_4_out, not_5_out, not_6_out, not_7_out, not_8_out, or_1_out, or_2_out, PCL_c;
  wire [0:0] Microcode_data_2;
  wire [1:0] multiplexer_3_out;
  wire [3:0] ALU_n, multiplexer_4_out, S, SC;
  wire [4:0] BS;
  wire [7:0] A, ABH, ABL, ALU_y, B, GP0, GP1, GP2, GP3, GP4, Instruction_Register_q, IR, multiplexer_5_out,
       multiplexer_6_out, multiplexer_7_out, O, PCH, PCL, rom_1_data, rom_2_data, rom_3_data, rom_4_data,
       rom_5_data, rom_6_data, rom_7_data, rom_8_data, ROM_Bank_0_data, SP, X, Y;
  wire [7:5] bankselect_1_alwaysq;
  wire [15:1] Microcode_data;

  Clock clock_1 (.out(clock_1_out));
  ROM #(.addrWidth(12), .dataWidth(16)) Microcode (.addr({IR, SC}), .data({Microcode_data, Microcode_data_2[0]}));
  Register8 Instruction_Register (
    .D(Instruction_Register_q), .Load(decoder_1_out2), .Enable(decoder_2_out2), .Clk(clock_1_out),
    .Reset(Reset), .Q(Instruction_Register_q), .AlwaysQ(IR));
  and and_1 (and_1_out, not_1_out, ABH[6]);
  and and_2 (and_2_out, decoder_1_out15, and_1_out);
  not not_1 (not_1_out, ABH[7]);
  // RGB_Video #(.cursor("No Cursor"), .scale(4)) rgb_video_1: pin names not known; wires that end beside it: Reset, clock_1_out, and_2_out, ABL[6:0], {ABH[5:0], ABL[7]}, Instruction_Register_q
  Increment4 StepCounter (.Reset(or_2_out), .Clk(clock_1_out), .O(SC));
  Multiplexer multiplexer_1 (.in0(1'b0), .in1(multiplexer_2_out), .out(multiplexer_1_out), .sel(decoder_3_out2));
  not not_2 (not_2_out, S[3]);
  not not_3 (not_3_out, S[2]);
  not not_4 (not_4_out, S[0]);
  Multiplexer #(.select(3)) multiplexer_2 (
    .in0(S[3]), .in1(not_2_out), .in2(not_3_out), .in3(not_4_out), .in4(S[2]), .in5(S[0]), .in6(S[1]),
    .in7(not_5_out), .out(multiplexer_2_out));  // open: sel
  not not_5 (not_5_out, S[1]);
  or or_1 (or_1_out, ABH[6], ABH[7]);
  not not_6 (not_6_out, or_1_out);
  and and_3 (and_3_out, not_6_out, decoder_1_out15);
  and and_4 (and_4_out, decoder_2_out15, not_6_out);
  or or_2 (or_2_out, Reset, multiplexer_1_out, decoder_3_out1);
  Demultiplexer demultiplexer_1 (
    .out0(demultiplexer_1_out0), .out1(demultiplexer_1_out1), .in(decoder_2_out0), .sel(Microcode_data[3]));
  Decoder #(.enable("false"), .select(4)) decoder_1 (
    .out0(decoder_1_out0), .out1(decoder_1_out1), .out2(decoder_1_out2), .out3(decoder_1_out3),
    .out4(decoder_1_out4), .out5(decoder_1_out5), .out6(decoder_1_out6), .out7(decoder_1_out7),
    .out8(decoder_1_out8), .out9(decoder_1_out9), .out10(decoder_1_out10), .out11(decoder_1_out11),
    .out12(decoder_1_out12), .out13(decoder_1_out13), .out14(decoder_1_out14), .out15(decoder_1_out15),
    .sel(Microcode_data[11:8]));
  Decoder #(.enable("false"), .select(4)) decoder_2 (
    .out0(decoder_2_out0), .out1(decoder_2_out1), .out2(decoder_2_out2), .out3(decoder_2_out3),
    .out4(decoder_2_out4), .out5(decoder_2_out5), .out6(decoder_2_out6), .out7(decoder_2_out7),
    .out8(decoder_2_out8), .out9(decoder_2_out9), .out10(decoder_2_out10), .out11(decoder_2_out11),
    .out12(decoder_2_out12), .out13(decoder_2_out13), .out14(decoder_2_out14), .out15(decoder_2_out15),
    .sel(Microcode_data[15:12]));
  Decoder #(.enable("false"), .select(2)) decoder_3 (
    .out1(decoder_3_out1), .out2(decoder_3_out2), .out3(decoder_3_out3), .sel(Microcode_data[2:1]));  // open: out0
  RAM #(.addrWidth(14), .databus("bidir"), .trigger("high"), .\type ("nonvolatile")) ram_1 (
    .addr({ABH[5:0], ABL}), .we(and_3_out), .oe(and_4_out), .data(Instruction_Register_q));
  Multiplexer #(.width(2)) multiplexer_3 (
    .in0({1'b0, Microcode_data_2[0]}), .in1(2'b10), .out(multiplexer_3_out), .sel(decoder_3_out2));
  Demultiplexer demultiplexer_2 (
    .out0(demultiplexer_2_out0), .out1(demultiplexer_2_out1), .in(decoder_1_out0), .sel(Microcode_data[3]));
  Demultiplexer demultiplexer_3 (
    .out0(demultiplexer_3_out0), .out1(demultiplexer_3_out1), .in(decoder_1_out1), .sel(Microcode_data[3]));
  assign Instruction_Register_q[0] = decoder_2_out1 ? decoder_2_out1 : 1'bz;  // Controlled_Buffer controlled_buffer_1
  assign Instruction_Register_q[1] = decoder_2_out1 ? 1'b0 : 1'bz;  // Controlled_Buffer controlled_buffer_2
  assign Instruction_Register_q[2] = decoder_2_out1 ? 1'b0 : 1'bz;  // Controlled_Buffer controlled_buffer_3
  assign Instruction_Register_q[3] = decoder_2_out1 ? 1'b0 : 1'bz;  // Controlled_Buffer controlled_buffer_4
  assign Instruction_Register_q[4] = decoder_2_out1 ? 1'b0 : 1'bz;  // Controlled_Buffer controlled_buffer_5
  assign Instruction_Register_q[5] = decoder_2_out1 ? 1'b0 : 1'bz;  // Controlled_Buffer controlled_buffer_6
  assign Instruction_Register_q[6] = decoder_2_out1 ? 1'b0 : 1'bz;  // Controlled_Buffer controlled_buffer_7
  assign Instruction_Register_q[7] = decoder_2_out1 ? 1'b0 : 1'bz;  // Controlled_Buffer controlled_buffer_8
  Hex_Digit_Display #(.decimalPoint("false")) hex_digit_display_1 (.value(PCH[7:4]));
  Hex_Digit_Display #(.decimalPoint("false")) hex_digit_display_2 (.value(PCH[3:0]));
  _7_Segment_Display #(.decimalPoint("false")) u_7_segment_display_1 (.b(S[3]), .c(S[3]));  // open: g, f, a, e, d
  _7_Segment_Display #(.decimalPoint("false")) u_7_segment_display_2 (.b(S[2]), .c(S[2]));  // open: g, f, a, e, d
  Hex_Digit_Display #(.decimalPoint("false")) hex_digit_display_3 (.value(X[7:4]));
  Hex_Digit_Display #(.decimalPoint("false")) hex_digit_display_4 (.value(GP2[7:4]));
  Hex_Digit_Display #(.decimalPoint("false")) hex_digit_display_5 (.value({3'b000, BS[4]}));
  Hex_Digit_Display #(.decimalPoint("false")) hex_digit_display_6 (.value(PCL[7:4]));
  Hex_Digit_Display #(.decimalPoint("false")) hex_digit_display_7 (.value(PCL[3:0]));
  _7_Segment_Display #(.decimalPoint("false")) u_7_segment_display_3 (.b(S[1]), .c(S[1]));  // open: g, f, a, e, d
  _7_Segment_Display #(.decimalPoint("false")) u_7_segment_display_4 (.b(S[0]), .c(S[0]));  // open: g, f, a, e, d
  Hex_Digit_Display #(.decimalPoint("false")) hex_digit_display_8 (.value(X[3:0]));
  Hex_Digit_Display #(.decimalPoint("false")) hex_digit_display_9 (.value(GP2[3:0]));
  Hex_Digit_Display #(.decimalPoint("false")) hex_digit_display_10 (.value(BS[3:0]));
  Hex_Digit_Display #(.decimalPoint("false")) hex_digit_display_11 (.value(ABH[7:4]));
  ProgramCounter u_PCL (
    .Cin(1'b0), .Inc(multiplexer_3_out), .Load(demultiplexer_2_out0), .Reset(Reset), .Clk(clock_1_out),
    .Address(Instruction_Register_q), .Enable(demultiplexer_1_out0), .C(PCL_c), .PC(Instruction_Register_q),
    .AlwaysQ(PCL));
  ProgramCounter u_PCH (
    .Cin(PCL_c), .Inc(2'b00), .Load(demultiplexer_2_out1), .Reset(Reset), .Clk(clock_1_out),
    .Address(Instruction_Register_q), .Enable(demultiplexer_1_out1), .PC(Instruction_Register_q),
    .AlwaysQ(PCH));  // open: C
  Register8 GP_Register1 (
    .D(Instruction_Register_q), .Load(decoder_1_out11), .Enable(decoder_2_out11), .Clk(clock_1_out),
    .Reset(Reset), .Q(Instruction_Register_q), .AlwaysQ(GP1));
  Register8 GP_Register2 (
    .D(Instruction_Register_q), .Load(decoder_1_out12), .Enable(decoder_2_out12), .Clk(clock_1_out),
    .Reset(Reset), .Q(Instruction_Register_q), .AlwaysQ(GP2));
  Register8 GP_Register3 (
    .D(Instruction_Register_q), .Load(decoder_1_out13), .Enable(decoder_2_out13), .Clk(clock_1_out),
    .Reset(Reset), .Q(Instruction_Register_q), .AlwaysQ(GP3));
  Register8 GP_Register4 (
    .D(Instruction_Register_q), .Load(decoder_1_out14), .Enable(decoder_2_out14), .Clk(clock_1_out),
    .Reset(Reset), .Q(Instruction_Register_q), .AlwaysQ(GP4));
  Hex_Digit_Display #(.decimalPoint("false")) hex_digit_display_12 (.value(ABH[3:0]));
  Hex_Digit_Display #(.decimalPoint("false")) hex_digit_display_13 (.value(ABL[7:4]));
  Hex_Digit_Display #(.decimalPoint("false")) hex_digit_display_14 (.value(O[7:4]));
  Hex_Digit_Display #(.decimalPoint("false")) hex_digit_display_15 (.value(O[3:0]));
  Hex_Digit_Display #(.decimalPoint("false")) hex_digit_display_16 (.value(Y[7:4]));
  Hex_Digit_Display #(.decimalPoint("false")) hex_digit_display_17 (.value(GP3[7:4]));
  Hex_Digit_Display #(.decimalPoint("false")) hex_digit_display_18 (.value(ABL[3:0]));
  Hex_Digit_Display #(.decimalPoint("false")) hex_digit_display_19 (.value(Y[3:0]));
  Hex_Digit_Display #(.decimalPoint("false")) hex_digit_display_20 (.value(GP3[3:0]));
  Hex_Digit_Display #(.decimalPoint("false")) hex_digit_display_21 (.value(SP[7:4]));
  Hex_Digit_Display #(.decimalPoint("false")) hex_digit_display_22 (.value(SP[3:0]));
  Hex_Digit_Display #(.decimalPoint("false")) hex_digit_display_23 (.value(A[7:4]));
  Hex_Digit_Display #(.decimalPoint("false")) hex_digit_display_24 (.value(A[3:0]));
  Hex_Digit_Display #(.decimalPoint("false")) hex_digit_display_25 (.value(GP0[7:4]));
  Hex_Digit_Display #(.decimalPoint("false")) hex_digit_display_26 (.value(GP0[3:0]));
  Hex_Digit_Display #(.decimalPoint("false")) hex_digit_display_27 (.value(GP4[7:4]));
  Hex_Digit_Display #(.decimalPoint("false")) hex_digit_display_28 (.value(GP4[3:0]));
  Register8 GP_Register0 (
    .D(Instruction_Register_q), .Load(decoder_1_out3), .Enable(decoder_2_out3), .Clk(clock_1_out),
    .Reset(Reset), .Q(Instruction_Register_q), .AlwaysQ(GP0));
  DataLatch8 ALU_out (
    .D(ALU_y), .Load(Microcode_data[4]), .Enable(decoder_2_out5), .Clk(clock_1_out),
    .Q(Instruction_Register_q), .AlwaysQ(O));
  ArithmeticLogicUnit ALU (
    .Opcode(Microcode_data[7:5]), .Cin(S[3]), .A(A), .B(B), .Ignore_Cin(Microcode_data[3]), .Y(ALU_y),
    .C(ALU_n[3]), .Z(ALU_n[2]), .O(ALU_n[1]), .N(ALU_n[0]));
  Register8 Accumulator (
    .D(Instruction_Register_q), .Load(decoder_1_out6), .Enable(decoder_2_out6), .Clk(clock_1_out),
    .Reset(Reset), .Q(Instruction_Register_q), .AlwaysQ(A));
  Register8 Y_Index (
    .D(Instruction_Register_q), .Load(decoder_1_out10), .Enable(decoder_2_out10), .Clk(clock_1_out),
    .Reset(Reset), .Q(Instruction_Register_q), .AlwaysQ(Y));
  not not_7 (not_7_out, ABH[7]);
  Hex_Digit_Display #(.decimalPoint("false")) hex_digit_display_29 (.value(IR[7:4]));
  Hex_Digit_Display #(.decimalPoint("false")) hex_digit_display_30 (.value(IR[3:0]));
  Hex_Digit_Display #(.decimalPoint("false")) hex_digit_display_31 (.value(B[7:4]));
  Hex_Digit_Display #(.decimalPoint("false")) hex_digit_display_32 (.value(B[3:0]));
  Hex_Digit_Display #(.decimalPoint("false")) hex_digit_display_33 (.value(GP1[7:4]));
  Hex_Digit_Display #(.decimalPoint("false")) hex_digit_display_34 (.value(GP1[3:0]));
  Hex_Digit_Display #(.decimalPoint("false")) hex_digit_display_35 (.value(SC));
  StackRegister8 Stack_Pointer (
    .D(Instruction_Register_q), .Load(decoder_1_out8), .Enable(decoder_2_out8), .Clk(clock_1_out),
    .Reset(Reset), .Q(Instruction_Register_q), .AlwaysQ(SP));
  Register4 Status (
    .D(multiplexer_4_out), .Load(Microcode_data[4]), .Enable(decoder_2_out4), .Clk(clock_1_out),
    .Reset(Reset), .Q(Instruction_Register_q[3:0]), .AlwaysQ(S));
  Register8 ALU_B (
    .D(Instruction_Register_q), .Load(decoder_1_out7), .Enable(decoder_2_out7), .Clk(clock_1_out),
    .Reset(Reset), .Q(Instruction_Register_q), .AlwaysQ(B));
  Register8 X_Index (
    .D(Instruction_Register_q), .Load(decoder_1_out9), .Enable(decoder_2_out9), .Clk(clock_1_out),
    .Reset(Reset), .Q(Instruction_Register_q), .AlwaysQ(X));
  not not_8 (not_8_out, ABH[6]);
  and and_5 (and_5_out, not_7_out, not_8_out, ABH[5], ABH[4], ABH[3], ABH[2], ABH[1], ABH[0], ABL[7], ABL[6], ABL[5], ABL[4], ABL[3], ABL[2], ABL[1], ABL[0]);
  BankSelect bankselect_1 (
    .D(Instruction_Register_q), .Load(and_5_out), .Enable(1'b0), .Clk(clock_1_out), .Reset(Reset),
    .AlwaysQ({bankselect_1_alwaysq, BS}));  // open: Q
  ROM #(.addrWidth(15)) ROM_Bank_0 (.addr({ABH[6:0], ABL}), .data(ROM_Bank_0_data));
  ROM #(.addrWidth(15)) rom_1 (.addr({ABH[6:0], ABL}), .data(rom_1_data));
  ROM #(.addrWidth(15)) rom_2 (.addr({ABH[6:0], ABL}), .data(rom_2_data));
  Multiplexer #(.width(4)) multiplexer_4 (
    .in0(ALU_n), .in1(Instruction_Register_q[3:0]), .out(multiplexer_4_out), .sel(decoder_1_out4));
  and and_6 (and_6_out, ABH[7], decoder_2_out15);
  ROM #(.addrWidth(15)) rom_3 (.addr({ABH[6:0], ABL}), .data(rom_3_data));
  ROM #(.addrWidth(15)) rom_4 (.addr({ABH[6:0], ABL}), .data(rom_4_data));
  Multiplexer #(.width(8)) multiplexer_5 (
    .in0({{7{1'b0}}, Microcode_data_2[0]}), .in1(Instruction_Register_q), .out(multiplexer_5_out),
    .sel(decoder_3_out3));
  Multiplexer #(.width(8)) multiplexer_6 (
    .in0(multiplexer_5_out), .in1({8{1'b0}}), .out(multiplexer_6_out), .sel(decoder_1_out5));
  assign Instruction_Register_q = and_6_out ? multiplexer_7_out : 8'bz;  // Controlled_Buffer controlled_buffer_9
  Multiplexer #(.select(5), .width(8)) multiplexer_7 (
    .in0(ROM_Bank_0_data), .in1(rom_1_data), .in2(rom_2_data), .in3(rom_3_data), .in4(rom_4_data),
    .in5(rom_5_data), .in6(rom_6_data), .in7(rom_7_data), .in8(rom_8_data), .out(multiplexer_7_out), .sel(BS));  // open: in9, in10, in11, in12, in13, in14, in15, in16, in17, in18, in19, in20, in21, in22, in23, in24, in25, in26, in27, in28, in29, in30, in31
  ROM #(.addrWidth(15)) rom_5 (.addr({ABH[6:0], ABL}), .data(rom_5_data));
  ROM #(.addrWidth(15)) rom_6 (.addr({ABH[6:0], ABL}), .data(rom_6_data));
  Address_Bus u_ABL (
    .Address(Instruction_Register_q), .Load(demultiplexer_3_out0), .Clk(clock_1_out), .Reset(Reset),
    .Cin(1'b0), .Inc(multiplexer_6_out), .O(ABL), .Cout(ABL_cout));
  Address_Bus u_ABH (
    .Address(Instruction_Register_q), .Load(demultiplexer_3_out1), .Clk(clock_1_out), .Reset(Reset),
    .Cin(ABL_cout), .Inc({8{1'b0}}), .O(ABH));  // open: Cout
  ROM #(.addrWidth(15)) rom_7 (.addr({ABH[6:0], ABL}), .data(rom_7_data));
  ROM #(.addrWidth(15)) rom_8 (.addr({ABH[6:0], ABL}), .data(rom_8_data));

  // Notes on the sheet:
  //   contents of Microcode (hex, n*v repeats v):
  //   100 108 f201 2 12*0 100 108 f201 f603 12*0 100 108 f201 f701 f108 7101 6f02 9*0 100 108 f201 f701
  //   f008 7002 10*0 100 108 f201 f700 5613 11*0 100 108 f201 f700 5673 11*0 100 108 f201 f700 56b3 11*0
  //   100 108 f201 f700 5693 11*0 100 108 f201 f700 5653 11*0 100 108 f201 f903 12*0 100 108 f201 fa03
  //   12*0 100 108 f201 6902 12*0 100 108 f201 6a02 12*0 100 108 f201 f701 f108 7100 9f00 7703 8*0 100 108
  //   f201 f701 f108 7100 af00 7703 8*0 100 108 f201 8902 12*0 100 108 f201 9602 12*0 100 108 f201 9802
  //   12*0 100 108 f201 a602 12*0 100 108 f201 f700 5633 11*0 100 108 f201 8100 1108 6f00 8600 1700 583a
  //   7*0 100 108 f201 8600 1700 5818 8100 1108 f602 7*0 100 108 f201 8100 1108 f08 8600 1700 5838 8100 0
  //   f00 8638 583a 0 0 100 108 f201 2700 4600 5472 26*0 100 108 f201 f701 f108 7100 f603 9*0 100 108 f201
  //   f701 f108 7100 f701 0 5612 7*0 100 108 f201 8600 1708 5818 8100 1108 f000 8608 5819 f009 7703 0 0 0
  //   100 108 f201 f701 f108 7100 f701 0 5632 7*0 100 108 f201 2700 4600 5472 10*0 100 108 f201 2204 f001
  //   f00a 10*0 100 108 f201 2224 f001 f00a 10*0 100 108 f201 2244 f001 f00a 10*0 100 108 f201 2264 f001
  //   f00a 10*0 100 108 f201 2284 f001 f00a 10*0 100 108 f201 22a4 f001 f00a 10*0 100 108 f201 22c4 f001
  //   f00a 10*0 100 108 f201 22e4 f001 f00a 10*0 100 108 f201 9600 1700 591a 10*0 100 108 f201 a600 1700
  //   5a1a 10*0 100 108 f201 2700 4600 54b2 10*0 100 108 f201 9600 1700 593a 10*0 100 108 f201 a600 1700
  //   5a3a 10*0 100 108 f201 f700 3b 11*0 100 108 f201 56da 12*0 100 108 f201 56fa 12*0 100 108 f201 56d2
  //   12*0 100 108 f201 56f2 12*0 100 108 f201 f701 f108 7100 f600 56d8 6f00 7703 6*0 100 108 f201 f701
  //   f108 7100 f600 56f8 6f00 7703 6*0 100 108 f201 f701 f108 7100 f600 56d0 6f00 7703 6*0 100 108 f201
  //   f701 f108 7100 f600 56f0 6f00 7703 6*0 100 108 f201 f700 9600 3b 10*0 100 108 f201 f700 a600 3b 10*0
  //   100 108 f201 f701 f108 7100 f701 9600 3a 7*0 100 108 f201 f701 f108 7100 f701 a600 3a 7*0 100 108
  //   f201 f701 f108 7100 f903 9*0 100 108 f201 f701 f108 7100 fa03 9*0 100 108 f201 f701 f108 7100 9906
  //   f603 8*0 100 108 f201 f701 f108 7100 aa06 f603 8*0 100 108 f201 f701 f108 7100 9906 f701 5672 7*0
  //   100 108 f201 f701 f108 7100 aa06 f701 5672 7*0 100 108 f201 f701 f108 7100 9907 0 6f02 7*0 100 108
  //   f201 f701 f108 7100 aa07 0 6f02 7*0 100 108 f201 1700 561a 11*0 100 108 f201 f701 f108 7100 f600
  //   1700 5f18 3 6*0 100 108 f201 f701 f108 7100 f701 f108 7100 6f00 3 5*0 100 108 f201 f701 f108 7100
  //   9906 f701 5612 7*0 100 108 f201 f701 f108 7100 aa06 f701 5612 7*0 100 108 f201 f700 561b 11*0 100
  //   108 f201 f700 563b 11*0 100 108 f201 f701 f108 7100 f701 0 561a 7*0 100 108 f201 f701 f108 7100 f701
  //   0 563a 7*0 100 108 f201 f303 12*0 100 108 f201 fb03 12*0 100 108 f201 fc03 12*0 100 108 f201 fd03
  //   12*0 100 108 f201 fe03 12*0 100 108 f201 f701 f108 7100 f303 9*0 100 108 f201 f701 f108 7100 fb03
  //   9*0 100 108 f201 f701 f108 7100 fc03 9*0 100 108 f201 f701 f108 7100 fd03 9*0 100 108 f201 f701 f108
  //   7100 fe03 9*0 100 108 f201 6302 12*0 100 108 f201 6b02 12*0 100 108 f201 6c02 12*0 100 108 f201 6d02
  //   12*0 100 108 f201 6e02 12*0 100 108 f201 3602 12*0 100 108 f201 b602 12*0 100 108 f201 c602 12*0 100
  //   108 f201 d602 12*0 100 108 f201 e602 12*0 100 108 f201 9302 12*0 100 108 f201 9b02 12*0 100 108 f201
  //   9c02 12*0 100 108 f201 9d02 12*0 100 108 f201 9e02 12*0 100 108 f201 3902 12*0 100 108 f201 b902
  //   12*0 100 108 f201 c902 12*0 100 108 f201 d902 12*0 100 108 f201 e902 12*0 100 108 f201 a302 12*0 100
  //   108 f201 ab02 12*0 100 108 f201 ac02 12*0 100 108 f201 ad02 12*0 100 108 f201 ae02 12*0 100 108 f201
  //   3a02 12*0 100 108 f201 ba02 12*0 100 108 f201 ca02 12*0 100 108 f201 da02 12*0 100 108 f201 ea02
  //   12*0 100 108 f201 f701 f108 7100 f701 f108 7100 f602
  //   C
  //   Z
  //   Program Counter
  //   Status
  //   O
  //   N
  //   X Index
  //   General Purpose 2
  //   Bank Select
  //   Address Bus
  //   ALU Out
  //   Y Index
  //   General Purpose 3
  //   Stack Pointer
  //   Accumulator
  //   General Purpose 0
  //   General Purpose 4
  //   Instruction
  //   ALU B
  //   General Purpose 1
  //   Step Counter
  //   contents of ROM_Bank_0 (hex, n*v repeats v):
  //   7d 83 7d 83 7d 83 7d 83 7d 83 7d 83 7e 82 7e 82 7e 82 7e 82 7e 82 7e 82 7e 82 7e 82 7e 82 7e 82 7e
  //   82 7e 82 7e 82 7e 82 7e 82 7e 82 7e 82 7e 82 7e 82 7e 82 7e 82 7e 82 7e 82 7e 82 7d 83 7d 83 7d 83
  //   7d 83 7d 83 7d 83 7d 83 7d 83 7d 83 7d 83 7d 83 7d 83 7d 83 7d 83 7d 83 7d 83 7d 83 7d 83 7d 83 7c
  //   84 7c 84 7c 84 7c 84 7c 84 7c 84 7c 84 7b 85 7b 85 7b 85 7b 85 7b 85 7b 85 7a 86 7a 86 7a 86 7a 86
  //   7a 86 7a 86 79 87 79 87 79 87 79 87 79 87 79 87 79 87 79 87 79 87 79 87 79 87 79 87 79 87 79 87 79
  //   87 79 87 79 87 79 87 75 81 3 87 75 82 2 87 79 87 79 87 79 87 7b 85 7c 84 7d 83 7f 81 33*7f 21 0
  //   37*7f 15 81 7f 81 7f 82 7e 82 7e 82 7e 82 7e 83 7d 83 7d 83 7d 83 7d 84 7c 84 7c 84 7c 84 7c 85 7b
  //   85 7b 85 7b 85 7b 85 6d 82 c 85 6d 82 c 85 6d 82 c 85 6d 82 d 84 6d 82 d 84 6e 82 c 84 a 81 64 81 c
  //   84 2 89 71 85 1 89 71 85 1 89 6e 81 2 8f 6e 81 2 8f 6e 81 2 8f 6e 82 2 8e 6e 82 2 8e 6e 82 2 8e 6e
  //   82 2 8e 6d 84 1 8e 6d 84 1 8e 6d 84 1 8e 6d 84 1 8e 6d 93 6d 93 6d 93 6c 94 6c 94 6c 94 6c 94 6c 94
  //   6c 94 6c 94 6d 93 6e 92 6e 92 6f 91 70 90 71 8f 71 8f 72 8e 73 8d 73 8d 74 8c 75 8b 75 8b 76 8a 76
  //   8a 77 89 77 89 78 88 78 88 78 88 79 87 79 87 7a 86 7a 86 7a 86 7a 86 7b 85 7b 85 7b 85 7b 85 7c 84
  //   7c 84 7c 84 7c 84 7d 83 7d 83 7d 83 7d 83 7d 83 7d 83 7d 83 7e 82 7e 82 0 75 8b 75 8b 75 8b 75 8b 75
  //   8b 75 8b 75 8b 75 8b 76 8a 76 8a 76 8a 76 8a 76 8a 76 8a 76 8a 76 8a 77 89 77 89 77 89 77 89 77 89
  //   78 88 78 88 78 88 78 88 78 88 78 88 78 88 79 87 79 87 79 87 79 87 79 87 79 87 79 87 79 87 79 87 79
  //   87 7a 86 7a 86 7b 85 7c 84 7c 84 7d 83 7e 82 7e 82 7e 82 7d 83 7b 85 79 87 77 89 76 8a 76 8a 76 8a
  //   76 8a 76 8a 76 8a 5c 81 19 8a 5c 82 18 8a 5d 82 17 8a 5e 81 18 89 5e 81 18 89 5e 81 18 89 77 89 5f
  //   81 17 89 5e 82 17 89 5f 81 17 89 77 89 77 89 78 88 78 88 78 88 60 81 2 81 14 88 60 81 2 82 13 88 63
  //   82 13 88 63 82 13 88 63 83 12 88 63 83 12 88 63 83 12 88 64 82 12 88 64 83 11 88 64 83 11 88 64 83
  //   12 87 65 82 12 87 65 82 12 87 66 82 11 87 66 82 11 87 66 82 11 87 66 83 10 87 67 82 10 87 68 81 10
  //   87 68 81 10 87 68 81 10 87 68 82 f 87 69 81 f 87 69 81 f 87 69 81 f 87 79 87 79 87 7a 86 7a 86 7a 86
  //   7a 86 7a 86 7a 86 7a 86 7a 86 7a 86 7a 86 7a 86 7a 86 7a 86 7a 86 7a 86 75 81 4 86 75 81 4 86 75 82
  //   3 86 75 8b 75 8b 75 8b 75 8b 75 8b 75 8b 75 8b 75 8b 75 8b 75 8b 75 8b 0 55 ab 55 ab 55 ab 55 ab 54
  //   ac 54 ac 54 ac 54 ac 54 ac 54 ac 54 ac 55 ab 55 ab 55 ab 55 ab 55 ab 55 ab 55 ab 55 ab 55 ab 55 ab
  //   55 ab 55 ab 55 ab 55 ab 55 ab 55 ab 55 ab 55 ab 55 ab 55 ab 55 ab 55 ab 55 ab 55 ab 55 ab 55 ab 55
  //   ab 55 ab 55 ab 55 ab 55 ab 56 aa 56 aa 56 aa 56 aa 57 a9 57 a9 57 a9 58 a8 58 a8 58 a8 58 a8 58 a8
  //   56 81 1 a8 56 81 2 a7 56 82 1 a7 56 aa 56 aa 56 aa 56 aa 56 aa 57 a9 57 a9 58 a8 58 a8 58 a8 57 a9
  //   57 a9 56 aa 55 ab 55 ab 55 ab 55 ab 56 aa 54 81 1 aa 54 81 1 aa 56 aa 56 aa 57 a9 56 aa 56 aa 56 aa
  //   56 aa 58 a8 59 a7 59 a7 59 a7 59 a7 5a a6 5a a6 5b a5 5b a5 5c a4 5c a4 5d a3 5d a3 5e a2 5e a2 5e
  //   a2 5f a1 5f a1 5f a1 60 a0 60 a0 61 9f 61 9f 61 9f 62 9e 62 9e 62 9e 63 9d 63 9d 64 9c 64 9c 64 9c
  //   65 9b 65 9b 66 9a 66 9a 66 9a 66 9a 67 99 68 98 69 97 6a 96 6b 95 6c 94 0 55 ab 55 ab 54 ac 54 ac 54
  //   ac 53 ad 53 ad 52 ae 52 ae 52 ae 51 af 51 af 50 b0 50 b0 4f b1 4f b1 4f b1 4e b2 4e b2 4d b3 4d b3
  //   4d b3 4d b3 4d b3 4d b3 4d b3 4d b3 4d b3 4d b3 4d b3 4d b3 4c b4 4c b4 4c b4 4c b4 4c b4 4c b4 4c
  //   b4 4c b4 4c b4 4c b4 4d b3 4d b3 4d b3 4d b3 4e b2 4e b2 4e b2 4b 82 1 b2 4f b1 53 ad 52 ae 52 ae 52
  //   ae 51 af 51 af 50 b0 50 b0 4f b1 4f b1 4e b2 4e b2 4d b3 4d b3 4d b3 4f b1 51 af 52 ae 54 ac 55 ab
  //   56 aa 57 a9 59 a7 59 a7 5b a5 5c a4 5c a4 5d a3 5e a2 5f a1 5f a1 60 a0 61 9f 61 9f 62 9e 62 9e 63
  //   9d 63 9d 64 9c 64 9c 64 9c 65 9b 65 9b 65 9b 65 9b 65 9b 66 9a 66 9a 66 9a 66 9a 66 9a 66 9a 66 9a
  //   66 9a 66 9a 66 9a 66 9a 66 9a 66 9a 66 9a 66 9a 66 9a 66 9a 66 9a 67 99 67 99 69 97 6a 96 6c 94 6d
  //   93 6e 92 6f 91 70 90 71 8f 71 8f 72 8e 73 8d 73 8d 0 5e a2 5d a3 5d a3 5d a3 57 81 4 a4 57 81 4 a4
  //   56 82 3 a5 56 81 4 a5 56 81 4 a5 55 82 3 a6 55 81 4 a6 55 81 3 a7 54 82 3 a7 54 82 2 a8 54 82 2 a8
  //   54 81 3 a8 53 82 2 a9 53 82 2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
  //   contents of rom_1 (hex, n*v repeats v):
  //   cf 12 ee 12 ef 12 ee 12 ee 13 81 3 ea 18 e8 19 e7 1a e3 1e e0 21 dd 23 dc 25 da 26 d9 28 d7 29 d6 2a
  //   d5 2c d3 2d d2 2e d2 2e d1 30 d0 30 cf 31 cf 31 ce 33 cd 33 cd 33 cd 33 cc 35 cb 35 cb 35 cb 36 c9
  //   37 c9 37 c8 38 c8 38 c9 38 c8 38 c8 38 c8 38 c8 38 c8 38 c9 38 c9 37 c9 37 c9 37 ca 36 cb 35 cc 34
  //   cd 33 cf 32 ce 32 ce 32 cd 33 cd 33 cc 34 cc 34 cc 34 cd 33 ce 32 ce 32 ce 32 c0 1 8e 31 c0 1 8f 30
  //   c1 7 89 2f c0 a 87 2f be d 86 2f bc f 87 2e bb 11 87 2d ba 12 87 2d b9 13 87 2d b9 13 88 2d b8 14 87
  //   2d b8 14 87 2d b7 15 87 2d b7 15 86 2e b7 15 87 2d b7 15 88 2c b7 15 87 2d b7 15 88 2c b8 13 89 2c
  //   b8 13 89 24 81 7 b8 14 88 24 81 7 b8 14 88 24 82 6 b8 15 87 24 82 2 81 3 b8 15 87 24 82 2 81 3 b9 15
  //   87 23 82 3 81 2 b9 15 87 24 82 2 81 2 ba 15 86 24 82 2 82 2 b9 15 86 24 82 2 82 2 ba 14 86 24 83 1
  //   83 1 ba 15 85 24 83 2 be 15 83 24 85 1 bf 14 83 24 85 1 c1 13 81 20 81 4 c8 33 81 4 c7 34 81 4 c7 34
  //   82 3 c7 34 83 2 c6 35 84 2 c5 36 83 2 c5 36 83 2 c4 37 84 1 c4 37 84 1 c4 38 83 1 c4 38 c8 38 c8 38
  //   c8 38 c7 39 c7 3a c6 3a c6 3a c6 3a c6 3a c6 3a c6 3b c5 3b c5 3b c5 3b c5 3b 89 3 b9 3b 87 5 b9 3b
  //   86 5 ba 12 81 29 84 5 ba 13 81 29 82 8 b9 13 81 32 ba 12 82 31 bb 12 83 2d 8b 0 d0 11 ef 11 ef 12 ee
  //   13 ee 12 ee 18 e9 18 e8 19 e3 1e e0 21 dd 23 dc 25 da 26 d8 29 d6 2a d6 2a d5 2c d3 2d d2 2e d2 2e
  //   d1 30 d0 30 cf 31 cf 31 ce 33 cd 33 cd 33 cc 34 cc 35 cb 35 cb 35 ca 37 c9 37 c9 37 c8 38 c9 37 c9
  //   38 c8 38 c8 38 c8 38 c8 38 c8 38 c9 38 c9 37 c9 37 c9 37 ca 36 cb 35 cc 34 cd 33 ce 33 ce 32 cd 33
  //   cd 33 cc 34 cc 34 cb 35 cc 34 cd 33 ce 32 ce 32 c1 1 8c 32 c1 1 8c 32 c1 1 82 4 88 30 c1 9 87 2f bf
  //   c 86 2f bd f 85 2f bc 10 85 2f bb 12 85 2e ba 13 86 2d ba 13 86 2e b8 14 87 2d b8 14 87 2d b8 14 87
  //   2d b8 14 87 2d b8 14 86 2e b8 14 87 2d b8 14 88 2c b8 14 87 2d b8 14 88 2c b8 14 88 2c b8 14 88 24
  //   81 7 b9 14 87 24 81 7 b9 14 87 24 82 6 b9 15 86 24 82 6 b9 15 86 24 82 2 81 3 ba 15 85 24 82 2 82 2
  //   ba 15 85 25 82 2 81 2 bb 14 86 24 82 2 82 2 ba 15 85 24 82 2 82 2 bb 14 85 24 83 1 83 1 bc 14 84 24
  //   83 1 83 1 bc 15 82 25 83 2 c1 13 81 25 81 1 83 1 c2 33 81 4 85 1 c2 33 81 4 c8 33 81 4 c7 34 82 3 c7
  //   34 83 2 c7 34 83 2 c6 35 84 2 c5 36 83 2 c5 36 83 2 c5 36 84 1 c5 36 84 1 c4 38 83 1 c4 38 c8 38 c8
  //   38 c8 38 c8 39 c7 39 c7 39 c7 39 c7 39 c6 3a c6 3a c6 3b c5 3b c5 3b c5 3b 88 4 b9 3b 87 4 ba 12 81
  //   28 86 5 ba 12 81 28 85 5 bb 11 82 29 82 8 ba 11 82 32 bb 11 82 31 bc 10 83 2e 8b 0 d0 11 ef 12 ee 12
  //   ef 12 ee 12 ee 17 ea 18 e8 19 e3 1e e0 21 dd 23 dc 25 da 26 d8 29 d6 2a d6 2a d5 2c d3 2d d2 2e d2
  //   2e d1 2f d1 30 cf 31 cf 31 ce 32 ce 33 cd 33 cc 34 cc 35 cb 35 cb 35 ca 36 ca 37 c8 38 c8 38 c9 37
  //   c9 38 c8 38 c8 38 c8 38 c8 38 c8 38 c9 38 c9 37 c9 37 ca 36 ca 36 cb 35 cc 34 cd 33 ce 33 ce 32 cd
  //   33 cd 33 cc 34 cb 35 cb 35 cc 34 cd 33 ce 32 ce 32 c1 1 8c 32 c1 1 8c 32 c1 8 87 30 c1 a 86 2f bf c
  //   86 2f bd f 85 2f bc 10 85 2f bb 12 85 2e ba 13 85 2e ba 13 86 2d ba 13 86 2d b9 14 87 2d b8 14 87 2d
  //   b8 14 87 2d b8 14 86 2e b8 14 86 2e b8 14 88 2c b8 14 87 2d b8 14 88 2c b8 14 88 2c b9 13 88 24 81 7
  //   b9 14 87 24 81 7 b9 15 86 24 81 7 b9 15 86 24 82 6 b9 15 86 24 82 2 81 3 ba 15 85 24 82 2 82 2 ba 15
  //   85 25 81 3 81 2 bb 14 86 24 82 2 82 2 ba 15 85 24 82 2 82 2 bb 15 84 24 83 1 82 2 bc 14 83 25 83 1
  //   83 1 bd 14 82 25 83 2 c1 13 81 25 81 1 83 1 c2 33 81 4 85 1 c2 33 81 4 c8 33 81 4 c7 34 81 4 c7 34
  //   83 2 c7 34 83 2 c6 35 84 2 c5 36 83 2 c5 36 83 2 c5 36 84 1 c5 36 84 1 c5 37 83 1 c5 37 c8 38 c8 38
  //   c8 38 c8 38 c8 39 c7 39 c7 39 c6 3a c6 3a c6 3a c6 3b c5 3b c5 3b c5 3b 88 4 b9 12 81 28 87 4 ba 12
  //   81 28 86 5 ba 11 82 28 85 5 bb 11 82 29 82 8 ba 11 82 32 bb 10 83 30 bd 10 83 2e 8b 0 d0 11 ef 11 ef
  //   12 ef 11 ef 12 ef 16 ea 18 e8 19 e4 1d e0 20 de 23 dc 24 db 26 d8 28 d7 2a d5 2b d5 2b d4 2d d2 2e
  //   d2 2e d1 2f d1 30 cf 31 cf 31 ce 32 ce 33 cd 33 cc 34 cc 35 cb 35 cb 35 ca 36 ca 37 c8 38 c8 38 c9
  //   37 c9 37 c9 38 c8 38 c8 38 c8 38 c8 38 c9 37 ca 37 c9 37 c9 37 ca 36 cb 35 cc 34 cd 33 ce 32 ce 33
  //   cd 33 cd 33 cc 34 cb 35 cb 35 cc 34 cd 33 ce 32 ce 32 c1 1 8c 32 c1 1 8c 32 c1 8 87 30 c0 b 86 2f be
  //   d 86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
  //   contents of rom_2 (hex, n*v repeats v):
  //   23*7f 50 84 7c 85 7a 86 7a 87 5 88 6d 86 4 8a 6c 85 4 8d 6a 84 4 8f 69 84 4 90 64 82 2 84 3 92 63 98
  //   1 86 61 97 4 85 60 97 6b 95 6b 95 6c 94 6e 94 6d 96 6b 97 6a 97 69 98 6b 95 6a 96 6b 97 69 99 63 83
  //   2 99 62 84 3 98 60 85 4 98 5f 86 3 97 60 85 4 97 60 85 4 98 60 85 2 97 63 84 2 92 6a 8f 6 81 6a 8f
  //   72 8e 72 8e 7 84 67 8f 4 86 67 8f 3 87 67 8f 3 87 67 90 1 88 67 90 1 88 67 99 68 84 1 93 69 83 2 92
  //   69 83 2 93 67 83 3 9b 5e 84 4 9d 5b 84 4 9d 5b 83 5 90 2 87 2 83 59 84 5 91 3 87 5c 83 5 9d 8 8b 47
  //   84 4 9d 5 92 44 83 5 b4 19 8a 20 84 4 b7 16 90 1b 83 4 b8 17 96 13 84 3 b9 17 9f 9 85 3 b9 18 ac 2
  //   bb 18 ea 1c e5 1c e4 1c 84 2 de 1c 83 6 8d 9 c5 28 8a d c1 2c 86 d c1 3f c1 3f 97 5 a5 40 96 7 a3 40
  //   87 6 89 8 a2 4e 88 a a0 4e 88 c 9e 4e 89 f 9a 4e 89 14 92 2 81 4e 83 2 84 18 8c 53 83 2 84 1b 89 54
  //   82 2 84 1c 81 1 87 53 82 3 83 1d 81 2 83 5a 82 1f 81 3 82 27*7f 20 0 24*7f 53 81 7c 84 7c 85 7b 87 4
  //   88 6d 87 3 8a 6c 86 3 8d 6b 84 4 8e 67 82 1 84 3 90 66 9d 63 95 3 85 64 94 6d 92 6e 92 70 91 70 92
  //   6f 93 6e 94 6d 94 6e 93 6c 97 6a 98 65 82 1 99 63 84 1 98 62 85 3 96 62 85 3 95 63 85 4 94 63 85 3
  //   92 67 85 2 90 6b 83 1 91 6c 8f 1 81 6f 8e 72 8e 7 81 6b 8d 5 84 6a 8d 3 86 6a 8e 2 86 6a 8e 1 87 6a
  //   96 6a 96 6b 83 2 90 6b 83 2 90 6b 83 3 95 64 84 3 9a 5f 83 4 9a 5f 83 4 8e 2 89 5f 83 5 8e 7 84 5f
  //   83 4 91 f 8d 4b 83 4 99 4 92 24 84 22 83 4 b0 22 8c 1a 83 4 b1 22 93 12 84 3 b2 23 9b 9 84 3 b3 22
  //   a8 2 b5 23 df 26 da 26 dc 25 83 3 89 7 c5 25 82 7 87 f bb 31 88 c bc 33 85 c bc 36 82 c 94 5 a3 44
  //   94 7 a0 46 84 8 88 7 9f 53 87 9 9e 52 87 c 9a 53 87 11 91 2 81 54 87 15 8c 58 82 2 84 17 89 58 82 2
  //   83 19 81 2 83 5a 82 3 82 1d 83 35*7f 2f 0 26*7f 53 83 7c 85 7 84 70 86 4 89 6d 86 4 8a 6c 85 4 8c 6a
  //   81 1 84 3 8f 68 99 67 93 3 85 65 93 6e 92 6f 91 70 90 72 90 71 91 70 92 6f 92 6e 92 6f 92 6b 82 1 96
  //   66 84 1 96 65 84 3 93 65 85 3 94 64 85 3 93 66 84 3 92 68 84 1 90 6d 82 1 8f 6e 92 6e 8d 74 8c 5 83
  //   6c 8c 3 85 6c 8c 3 85 6c 8d 1 86 6c 94 6c 94 6d 83 1 8f 6d 83 2 8e 6d 82 3 92 68 83 4 97 62 83 4 98
  //   60 83 4 8d 3 88 61 83 4 8e 5 84 8 88 51 83 4 91 a 90 2b 83 20 83 3 ad 29 8b 18 83 3 ae 29 92 11 83 2
  //   af 2a 9a 7 84 1 b1 2a d7 2b d7 2d d3 2d 8c 2 c7 2b 83 3 88 c ba 34 86 f b7 36 85 e b7 38 85 c b7 3a
  //   84 c 92 6 9e 3c 81 d 84 7 87 7 9d 56 86 9 9b 56 87 b 97 57 87 10 8f 5a 82 1 84 14 8a 5b 82 2 83 16
  //   88 5b 82 2 83 17 81 2 82 62 81 1d 81 39*7f 37 0 28*7f 55 82 8 86 6f 86 4 88 6e 85 4 8a 6e 84 3 8c 6c
  //   95 6b 91 2 83 6a 91 3 83 6a 90 71 8f 72 8e 73 8f 73 8f 72 8f 72 8f 71 8f 6e 82 2 8e 6d 84 3 8c 6d 84
  //   3 8e 6b 84 3 8f 6a 84 3 90 6b 83 1 91 6c 82 1 91 6c 93 6d 8c 1 82 2 81 6f 8b 3 83 6f 8b 2 84 6f 8b 2
  //   84 6f 91 70 90 70 82 2 8c 70 82 2 8c 6f 83 3 8d 6d 83 3 91 69 82 4 95 64 83 3 8b 2 83 3 83 64 82 3
  //   8d 2 84 7 8c 54 83 3 8f 2 84 1 91 34 89 16 82 2 aa 33 90 e 83 1 aa 34 99 4 b0 34 cd 38 ca 36 cb 36
  //   82 3 86 b b4 3d 85 d b0 3f 84 d b1 3f 84 c b1 41 83 c 87 1 a8 42 83 15 8a 3 99 43 81 16 86 9 97 5a
  //   87 d 91 5b 87 11 8a 5f 82 1 83 13 87 60 82 1 82 17 83 46*7f 44 0 28*7f 56 81 8 85 71 85 4 87 70 85 3
  //   89 70 83 3 8b 6d 94 6c 90 2 83 6c 8f 4 82 6c 8e 73 8d 74 8d 75 8e 73 8e 73 8e 72 8f 6e 82 2 8d 6f 83
  //   2 8b 6f 84 3 8b 6e 84 3 8c 6e 83 3 8d 6e 83 1 8f 6e 82 1 8f 6e 92 6f 8a 2 85 6f 8a 3 83 70 8a 2 84
  //   70 8b 1 84 70 90 71 82 1 8c 71 82 2 8b 70 83 2 8d 6e 82 4 8f 6b 82 3 93 67 82 4 8b 1 82 3 83 66 82 3
  //   90 7 8c 3a 84 19 82 3 93 1 91 39 8b 11 83 3 a5 39 92 a 83 2 a6 3a 9e 1 a8 3b c7 3c c5 3b 83 2 87 5
  //   b5 42 84 c ad 45 83 b ad 46 83 a ae 46 83 a 86 2 a5 47 81 15 86 1 81 3 97 5e 85 9 95 5d 85 e 8f 5e
  //   86 11 88 61 82 1 82 13 86 62 82 1 82 16 82 49*7f 4a 0 28*7f 56 82 7e 84 4 86 72 84 3 88 72 83 2 8a
  //   6f 92 6e 8f 2 82 6e 8e 3 82 6e 8c 75 8c 75 8d 75 8c 75 8c 74 8d 71 81 1 8d 70 83 2 8b 6f 84 3 8b 6f
  //   83 3 8c 6e 83 2 8e 6f 82 1 8e 6f 91 70 89 4 82 71 89 3 83 71 89 2 84 71 8a 1 84 71 8f 72 82 1 8b 72
  //   82 1 8b 71 82 3 8f 6c 82 3 92 68 82 4 89 2 83 3 81 68 82 3 8c 1 83 6 89 5c 81 3 a1 40 88 12 82 2 a3
  //   3f 90 9 83 2 a3 40 c1 41 c0 42 bf 42 81 4 86 7 ad 49 85 8 a9 4d 82 8 aa 57 8d 4 98 60 85 5 95 61 85
  //   7 9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
  //   contents of rom_3 (hex, n*v repeats v):
  //   ed 13 ee 12 f0 10 f1 f f3 d f4 c c1 1 b3 b c1 1 b4 a c0 2 b6 8 c0 1 b8 7 c0 1 b9 6 bc 6 b9 5 bb a b8
  //   3 bb b b8 2 bb b f5 b f5 b f5 b f5 a f5 b f6 a f5 b f5 b f5 b f5 a f6 a f6 a f6 9 f7 9 f8 8 f8 8 f8
  //   8 f8 8 f8 8 f8 8 f7 9 f7 9 f7 9 f6 b f5 b f4 c f4 d f6 a fa 4 85*ff 92 0 5*ff c2 1 ff 1 82 1 fb 6 fa
  //   8 f7 9 f6 a f6 a f6 a f5 c f5 b f5 b f5 b f6 b f5 b f5 b f5 b f6 a f6 a f6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
  //   contents of rom_4 (hex, n*v repeats v):
  //   9*ff e9 4 e4 b 8c 5 df 11 8a 6 dc 16 87 7 db 18 85 8 da 1a 83 9 d9 1b 82 b d8 28 d7 29 d7 2a d5 2b
  //   d5 2c d4 2c d4 2d d2 2f d1 30 d0 2f d1 2d d3 2a d6 2a d6 2a d6 2a d6 2a d6 2a d6 2a d6 21 82 7 d5 23
  //   83 4 d5 25 84 2 d4 27 d7 29 d7 29 d7 29 d7 29 d7 28 d8 27 db 25 dc 24 dd 22 e1 1f e2 1e e2 1e e2 1f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
  //   contents of rom_5 (hex, n*v repeats v):
  //   8*7f 49 81 7d 83 7d 84 7c 85 7b 85 7b 85 7b 85 79 88 78 89 78 88 78 87 79 87 79 87 79 87 79 86 7a 86
  //   7a 87 79 86 7a 85 7b 85 7b 85 7b 85 7b 85 7b 85 7b 85 7b 85 7b 85 7b 85 7b 85 7b 85 7b 85 7b 85 7a
  //   86 7a 86 7a 87 77 89 74 8d 72 8e 71 90 6f 92 6d 95 6b 95 6a 97 69 97 68 99 67 99 66 9a 66 9a 65 9b 6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
  //   contents of rom_6 (hex, n*v repeats v):
  //   6*7f 53 89 75 8e 70 92 6d 95 6a 97 68 99 66 9b 64 9c 63 9e 62 9f 60 a0 60 a1 5e a2 5e a2 5e a3 5b a5
  //   5a a6 59 a7 59 a7 59 a7 5a a6 5a a6 5a a6 5a a6 5a a5 5b a5 5a a6 59 a7 58 a9 57 a9 56 ab 54 ac 53
  //   ae 52 af 52 af 52 83 3 a9 57 a9 57 a4 3 82 58 a3 5e 82 1 9f 62 9f 62 9b 2 81 39 83 25 9d 3a 85 24 9d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
  //   contents of rom_7 (hex, n*v repeats v):
  //   6*7f 3f 87 1 85 71 91 6d 95 6a 97 68 99 67 99 66 9b 65 9b 65 9c 63 9d 2 83 5e 9d 1 87 5b a6 5a a6 5a
  //   a6 5a a6 5a a7 59 a7 59 a7 59 a7 59 a7 59 a7 59 a7 58 a8 58 a8 56 ab 54 ac 54 a2 1 88 54 a3 1 87 55
  //   a3 1 87 56 a1 2 87 57 a0 2 87 58 9f 2 88 58 81 1 9c 2 88 5a 9c 2 88 5a 9c 2 88 59 a7 58 9e 1 8a 59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
  //   contents of rom_8 (hex, n*v repeats v):
  //   3f 95 6b 96 6a 96 6a 97 20 81 49 96 6a 97 6a 96 6b 8c 2 88 6a 8b 3 89 6a 89 5 88 6c 85 7 88 79 88 79
  //   88 78 88 79 88 79 87 79 88 79 88 79 88 78 88 79 89 78 89 78 89 78 8a 77 8a 78 8a 77 8a 78 8a 79 88
  //   7a 87 7b 86 7c 85 7c 85 7d 84 7d 83 7e 83 7e 82 7e 82 9*7f 64 84 3f 84 38 85 3f 85 34 88 3e 86 32 8a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
endmodule

module ArithmeticLogicUnit (
  input  [2:0] Opcode,
  input  Cin,
  input  [7:0] A,
  input  [7:0] B,
  input  Ignore_Cin,
  output [7:0] Y,
  output C,
  output Z,
  output O,
  output N
);

  wire and_1_out, and_2_out, and_3_out, and_4_out, and_5_out, and_6_out, cla8_1_c0, multiplexer_2_out,
       multiplexer_3_out, multiplexer_4_out, not_1_out, not_2_out, not_3_out, not_4_out, not_5_out,
       not_6_out, not_7_out, not_8_out, not_9_out, not_10_out, not_11_out, not_12_out, not_13_out, xor_1_out,
       xor_2_out;
  wire [0:0] multiplexer_1_out;
  wire [7:0] and_8_out, cla8_1_sum, multiplexer_5_out, negate8_1_nega, not_14_out, or_2_out, xor_3_out;

  not not_1 (not_1_out, Opcode[0]);
  and and_1 (and_1_out, not_1_out, Opcode[1], Opcode[2]);
  and and_2 (and_2_out, and_1_out, A[7]);
  and and_3 (and_3_out, Opcode[0], Opcode[1], Opcode[2]);
  // Probe on A
  // Probe on A
  // Probe on A
  // Probe on B
  // Probe on B
  // Probe on B
  not not_2 (not_2_out, Opcode[1]);
  not not_3 (not_3_out, Opcode[2]);
  and and_4 (and_4_out, not_2_out, not_3_out);
  and and_5 (and_5_out, and_3_out, A[0]);
  and and_6 (and_6_out, and_4_out, cla8_1_c0);
  or or_1 (C, and_2_out, and_5_out, and_6_out);
  xor xor_1 (xor_1_out, A[7], B[7]);
  not not_4 (not_4_out, N);
  not not_5 (not_5_out, Y[6]);
  not not_6 (not_6_out, Y[5]);
  not not_7 (not_7_out, Y[4]);
  and and_7 (Z, not_4_out, not_5_out, not_6_out, not_7_out, not_9_out, not_10_out, not_11_out, not_12_out);
  Multiplexer multiplexer_1 (.in0(Cin), .in1(1'b0), .out(multiplexer_1_out[0]), .sel(Ignore_Cin));
  not not_8 (not_8_out, xor_1_out);
  Multiplexer multiplexer_2 (.in0(not_8_out), .in1(xor_1_out), .out(multiplexer_2_out), .sel(Opcode[0]));
  not not_9 (not_9_out, Y[3]);
  not not_10 (not_10_out, Y[2]);
  not not_11 (not_11_out, Y[1]);
  not not_12 (not_12_out, Y[0]);
  and and_8 (and_8_out[0], A[0], B[0]);
  and and_9 (and_8_out[1], A[1], B[1]);
  and and_10 (and_8_out[2], A[2], B[2]);
  and and_11 (and_8_out[3], A[3], B[3]);
  and and_12 (and_8_out[4], A[4], B[4]);
  and and_13 (and_8_out[5], A[5], B[5]);
  and and_14 (and_8_out[6], A[6], B[6]);
  and and_15 (and_8_out[7], A[7], B[7]);
  or or_2 (or_2_out[0], A[0], B[0]);
  or or_3 (or_2_out[1], A[1], B[1]);
  or or_4 (or_2_out[2], A[2], B[2]);
  or or_5 (or_2_out[3], A[3], B[3]);
  or or_6 (or_2_out[4], A[4], B[4]);
  or or_7 (or_2_out[5], A[5], B[5]);
  or or_8 (or_2_out[6], A[6], B[6]);
  or or_9 (or_2_out[7], A[7], B[7]);
  xor xor_2 (xor_2_out, A[7], N);
  and and_16 (O, multiplexer_2_out, xor_2_out);
  Negate8 negate8_1 (.A(B), .NegA(negate8_1_nega));
  Multiplexer multiplexer_3 (.in0(Cin), .in1(not_13_out), .out(multiplexer_3_out), .sel(Opcode[0]));
  not not_13 (not_13_out, Cin);
  Multiplexer multiplexer_4 (.in0(multiplexer_3_out), .in1(1'b0), .out(multiplexer_4_out), .sel(Ignore_Cin));
  Multiplexer #(.width(8)) multiplexer_5 (.in0(B), .in1(negate8_1_nega), .out(multiplexer_5_out), .sel(Opcode[0]));
  not not_14 (not_14_out[0], A[0]);
  not not_15 (not_14_out[1], A[1]);
  not not_16 (not_14_out[2], A[2]);
  not not_17 (not_14_out[3], A[3]);
  not not_18 (not_14_out[4], A[4]);
  not not_19 (not_14_out[5], A[5]);
  not not_20 (not_14_out[6], A[6]);
  not not_21 (not_14_out[7], A[7]);
  xor xor_3 (xor_3_out[0], A[0], B[0]);
  xor xor_4 (xor_3_out[1], A[1], B[1]);
  xor xor_5 (xor_3_out[2], A[2], B[2]);
  xor xor_6 (xor_3_out[3], A[3], B[3]);
  xor xor_7 (xor_3_out[4], A[4], B[4]);
  xor xor_8 (xor_3_out[5], A[5], B[5]);
  xor xor_9 (xor_3_out[6], A[6], B[6]);
  xor xor_10 (xor_3_out[7], A[7], B[7]);
  CLA8 cla8_1 (.A(A), .B(multiplexer_5_out), .Cin(multiplexer_4_out), .C0(cla8_1_c0), .Sum(cla8_1_sum));
  Multiplexer #(.select(3), .width(8)) multiplexer_6 (
    .in0(cla8_1_sum), .in1(cla8_1_sum), .in2(not_14_out), .in3(and_8_out), .in4(xor_3_out), .in5(or_2_out),
    .in6({A[6:0], multiplexer_1_out[0]}), .in7({multiplexer_1_out[0], A[7:1]}), .out({N, Y[6:0]}),
    .sel(Opcode));
  // Probe on {N, Y[6:0]}
  // Probe on {N, Y[6:0]}
  // Probe on {N, Y[6:0]}

  assign Y[7] = N;

  // Notes on the sheet:
  //   Status Flags
endmodule

module ProgramCounter (
  input  Cin,
  input  [1:0] Inc,
  input  Load,
  input  Reset,
  input  Clk,
  input  [7:0] Address,
  input  Enable,
  output C,
  output [7:0] PC,
  output [7:0] AlwaysQ
);

  wire [7:0] cla8_1_sum, multiplexer_1_out, register8_1_q;

  CLA8 cla8_1 (.A(register8_1_q), .B({{6{1'b0}}, Inc}), .Cin(Cin), .C0(C), .Sum(cla8_1_sum));
  Multiplexer #(.width(8)) multiplexer_1 (.in0(cla8_1_sum), .in1(Address), .out(multiplexer_1_out), .sel(Load));
  Register8 register8_1 (
    .D(multiplexer_1_out), .Load(1'b1), .Enable(1'b1), .Clk(Clk), .Reset(Reset), .Q(register8_1_q),
    .AlwaysQ(AlwaysQ));
  assign PC = Enable ? register8_1_q : 8'bz;  // Controlled_Buffer controlled_buffer_1
endmodule

module Address_Bus (
  input  [7:0] Address,
  input  Load,
  input  Clk,
  input  Reset,
  input  Cin,
  input  [7:0] Inc,
  output [7:0] O,
  output Cout
);

  wire [7:0] cla8_1_sum, multiplexer_1_out;

  Multiplexer #(.width(8)) multiplexer_1 (.in0(cla8_1_sum), .in1(Address), .out(multiplexer_1_out), .sel(Load));
  CLA8 cla8_1 (.A(O), .B(Inc), .Cin(Cin), .C0(Cout), .Sum(cla8_1_sum));
  Register8 register8_1 (
    .D(multiplexer_1_out), .Load(1'b1), .Enable(1'b1), .Clk(Clk), .Reset(Reset), .Q(O));  // open: AlwaysQ
endmodule

module Increment8 (
  input  Reset,
  input  Clk,
  input  Cin,
  input  Inc,
  output [7:0] O
);

  wire [7:0] cla8_1_sum;

  CLA8 cla8_1 (.A(O), .B({{7{1'b0}}, Inc}), .Cin(Cin), .Sum(cla8_1_sum));  // open: C0
  Register8 register8_1 (.D(cla8_1_sum), .Load(1'b1), .Enable(1'b1), .Clk(Clk), .Reset(Reset), .Q(O));  // open: AlwaysQ
endmodule

module Increment4 (
  input  Reset,
  input  Clk,
  output [3:0] O
);

  wire d_flipflop_1_q, undriven;
  wire [3:0] cla4_1_sum;

  D_FlipFlop d_flipflop_1 (.D(Reset), .Clk(Clk), .Reset(undriven), .Q(d_flipflop_1_q));  // open: Qbar
  CLA4 cla4_1 (.A(O), .B(4'b0001), .Sum(cla4_1_sum));  // open: Cin, Cout, PG, GG
  D_FlipFlop d_flipflop_2 (.D(cla4_1_sum[0]), .Clk(Clk), .Reset(d_flipflop_1_q), .Q(O[0]));  // open: Qbar
  D_FlipFlop d_flipflop_3 (.D(cla4_1_sum[1]), .Clk(Clk), .Reset(d_flipflop_1_q), .Q(O[1]));  // open: Qbar
  D_FlipFlop d_flipflop_4 (.D(cla4_1_sum[2]), .Clk(Clk), .Reset(d_flipflop_1_q), .Q(O[2]));  // open: Qbar
  D_FlipFlop d_flipflop_5 (.D(cla4_1_sum[3]), .Clk(Clk), .Reset(d_flipflop_1_q), .Q(O[3]));  // open: Qbar
endmodule

module Register8 (
  input  [7:0] D,
  input  Load,
  input  Enable,
  input  Clk,
  input  Reset,
  output [7:0] Q,
  output [7:0] AlwaysQ
);

  wire multiplexer_1_out, multiplexer_2_out, multiplexer_3_out, multiplexer_4_out, multiplexer_5_out,
       multiplexer_6_out, multiplexer_7_out, multiplexer_8_out;

  Multiplexer multiplexer_1 (.in0(AlwaysQ[0]), .in1(D[0]), .out(multiplexer_1_out), .sel(Load));
  Multiplexer multiplexer_2 (.in0(AlwaysQ[1]), .in1(D[1]), .out(multiplexer_2_out), .sel(Load));
  Multiplexer multiplexer_3 (.in0(AlwaysQ[2]), .in1(D[2]), .out(multiplexer_3_out), .sel(Load));
  Multiplexer multiplexer_4 (.in0(AlwaysQ[3]), .in1(D[3]), .out(multiplexer_4_out), .sel(Load));
  Multiplexer multiplexer_5 (.in0(AlwaysQ[4]), .in1(D[4]), .out(multiplexer_5_out), .sel(Load));
  Multiplexer multiplexer_6 (.in0(AlwaysQ[5]), .in1(D[5]), .out(multiplexer_6_out), .sel(Load));
  Multiplexer multiplexer_7 (.in0(AlwaysQ[6]), .in1(D[6]), .out(multiplexer_7_out), .sel(Load));
  Multiplexer multiplexer_8 (.in0(AlwaysQ[7]), .in1(D[7]), .out(multiplexer_8_out), .sel(Load));
  D_FlipFlop d_flipflop_1 (.D(multiplexer_1_out), .Clk(Clk), .Reset(Reset), .Q(AlwaysQ[0]));  // open: Qbar
  D_FlipFlop d_flipflop_2 (.D(multiplexer_2_out), .Clk(Clk), .Reset(Reset), .Q(AlwaysQ[1]));  // open: Qbar
  D_FlipFlop d_flipflop_3 (.D(multiplexer_3_out), .Clk(Clk), .Reset(Reset), .Q(AlwaysQ[2]));  // open: Qbar
  D_FlipFlop d_flipflop_4 (.D(multiplexer_4_out), .Clk(Clk), .Reset(Reset), .Q(AlwaysQ[3]));  // open: Qbar
  D_FlipFlop d_flipflop_5 (.D(multiplexer_5_out), .Clk(Clk), .Reset(Reset), .Q(AlwaysQ[4]));  // open: Qbar
  D_FlipFlop d_flipflop_6 (.D(multiplexer_6_out), .Clk(Clk), .Reset(Reset), .Q(AlwaysQ[5]));  // open: Qbar
  D_FlipFlop d_flipflop_7 (.D(multiplexer_7_out), .Clk(Clk), .Reset(Reset), .Q(AlwaysQ[6]));  // open: Qbar
  D_FlipFlop d_flipflop_8 (.D(multiplexer_8_out), .Clk(Clk), .Reset(Reset), .Q(AlwaysQ[7]));  // open: Qbar
  assign Q = Enable ? AlwaysQ : 8'bz;  // Controlled_Buffer controlled_buffer_1
endmodule

module DataLatch8 (
  input  [7:0] D,
  input  Load,
  input  Enable,
  input  Clk,
  output [7:0] Q,
  output [7:0] AlwaysQ
);

  wire and_1_out, not_1_out;

  and and_1 (and_1_out, Load, not_1_out);
  not not_1 (not_1_out, Clk);
  D_Latch d_latch_1 (.D(D[0]), .Enable(and_1_out), .Q(AlwaysQ[0]));  // open: Qbar
  D_Latch d_latch_2 (.D(D[1]), .Enable(and_1_out), .Q(AlwaysQ[1]));  // open: Qbar
  D_Latch d_latch_3 (.D(D[2]), .Enable(and_1_out), .Q(AlwaysQ[2]));  // open: Qbar
  D_Latch d_latch_4 (.D(D[3]), .Enable(and_1_out), .Q(AlwaysQ[3]));  // open: Qbar
  D_Latch d_latch_5 (.D(D[4]), .Enable(and_1_out), .Q(AlwaysQ[4]));  // open: Qbar
  D_Latch d_latch_6 (.D(D[5]), .Enable(and_1_out), .Q(AlwaysQ[5]));  // open: Qbar
  D_Latch d_latch_7 (.D(D[6]), .Enable(and_1_out), .Q(AlwaysQ[6]));  // open: Qbar
  D_Latch d_latch_8 (.D(D[7]), .Enable(and_1_out), .Q(AlwaysQ[7]));  // open: Qbar
  assign Q = Enable ? AlwaysQ : 8'bz;  // Controlled_Buffer controlled_buffer_1
endmodule

module Register4 (
  input  [3:0] D,
  input  Load,
  input  Enable,
  input  Clk,
  input  Reset,
  output [3:0] Q,
  output [3:0] AlwaysQ
);

  wire multiplexer_1_out, multiplexer_2_out, multiplexer_3_out, multiplexer_4_out;

  Multiplexer multiplexer_1 (.in0(AlwaysQ[0]), .in1(D[0]), .out(multiplexer_1_out), .sel(Load));
  Multiplexer multiplexer_2 (.in0(AlwaysQ[1]), .in1(D[1]), .out(multiplexer_2_out), .sel(Load));
  Multiplexer multiplexer_3 (.in0(AlwaysQ[2]), .in1(D[2]), .out(multiplexer_3_out), .sel(Load));
  Multiplexer multiplexer_4 (.in0(AlwaysQ[3]), .in1(D[3]), .out(multiplexer_4_out), .sel(Load));
  D_FlipFlop d_flipflop_1 (.D(multiplexer_1_out), .Clk(Clk), .Reset(Reset), .Q(AlwaysQ[0]));  // open: Qbar
  D_FlipFlop d_flipflop_2 (.D(multiplexer_2_out), .Clk(Clk), .Reset(Reset), .Q(AlwaysQ[1]));  // open: Qbar
  D_FlipFlop d_flipflop_3 (.D(multiplexer_3_out), .Clk(Clk), .Reset(Reset), .Q(AlwaysQ[2]));  // open: Qbar
  D_FlipFlop d_flipflop_4 (.D(multiplexer_4_out), .Clk(Clk), .Reset(Reset), .Q(AlwaysQ[3]));  // open: Qbar
  assign Q = Enable ? AlwaysQ : 4'bz;  // Controlled_Buffer controlled_buffer_1
endmodule

module StackRegister8 (
  input  [7:0] D,
  input  Load,
  input  Enable,
  input  Clk,
  input  Reset,
  output [7:0] Q,
  output [7:0] AlwaysQ
);

  wire multiplexer_1_out, multiplexer_2_out, multiplexer_3_out, multiplexer_4_out, multiplexer_5_out,
       multiplexer_6_out, multiplexer_7_out, multiplexer_8_out, multiplexer_9_out, multiplexer_10_out,
       multiplexer_11_out, multiplexer_12_out, multiplexer_13_out, multiplexer_14_out, multiplexer_15_out,
       multiplexer_16_out;

  Multiplexer multiplexer_1 (.in0(AlwaysQ[0]), .in1(D[0]), .out(multiplexer_1_out), .sel(Load));
  Multiplexer multiplexer_2 (.in0(AlwaysQ[1]), .in1(D[1]), .out(multiplexer_2_out), .sel(Load));
  Multiplexer multiplexer_3 (.in0(AlwaysQ[2]), .in1(D[2]), .out(multiplexer_3_out), .sel(Load));
  Multiplexer multiplexer_4 (.in0(AlwaysQ[3]), .in1(D[3]), .out(multiplexer_4_out), .sel(Load));
  Multiplexer multiplexer_5 (.in0(AlwaysQ[4]), .in1(D[4]), .out(multiplexer_5_out), .sel(Load));
  Multiplexer multiplexer_6 (.in0(AlwaysQ[5]), .in1(D[5]), .out(multiplexer_6_out), .sel(Load));
  Multiplexer multiplexer_7 (.in0(AlwaysQ[6]), .in1(D[6]), .out(multiplexer_7_out), .sel(Load));
  Multiplexer multiplexer_8 (.in0(AlwaysQ[7]), .in1(D[7]), .out(multiplexer_8_out), .sel(Load));
  Multiplexer multiplexer_9 (.in0(multiplexer_1_out), .in1(1'b1), .out(multiplexer_9_out), .sel(Reset));
  Multiplexer multiplexer_10 (.in0(multiplexer_2_out), .in1(1'b1), .out(multiplexer_10_out), .sel(Reset));
  Multiplexer multiplexer_11 (.in0(multiplexer_3_out), .in1(1'b1), .out(multiplexer_11_out), .sel(Reset));
  Multiplexer multiplexer_12 (.in0(multiplexer_4_out), .in1(1'b1), .out(multiplexer_12_out), .sel(Reset));
  Multiplexer multiplexer_13 (.in0(multiplexer_5_out), .in1(1'b1), .out(multiplexer_13_out), .sel(Reset));
  Multiplexer multiplexer_14 (.in0(multiplexer_6_out), .in1(1'b1), .out(multiplexer_14_out), .sel(Reset));
  Multiplexer multiplexer_15 (.in0(multiplexer_7_out), .in1(1'b1), .out(multiplexer_15_out), .sel(Reset));
  Multiplexer multiplexer_16 (.in0(multiplexer_8_out), .in1(1'b1), .out(multiplexer_16_out), .sel(Reset));
  D_FlipFlop d_flipflop_1 (.D(multiplexer_9_out), .Clk(Clk), .Q(AlwaysQ[0]));  // open: Reset, Qbar
  D_FlipFlop d_flipflop_2 (.D(multiplexer_10_out), .Clk(Clk), .Q(AlwaysQ[1]));  // open: Reset, Qbar
  D_FlipFlop d_flipflop_3 (.D(multiplexer_11_out), .Clk(Clk), .Q(AlwaysQ[2]));  // open: Reset, Qbar
  D_FlipFlop d_flipflop_4 (.D(multiplexer_12_out), .Clk(Clk), .Q(AlwaysQ[3]));  // open: Reset, Qbar
  D_FlipFlop d_flipflop_5 (.D(multiplexer_13_out), .Clk(Clk), .Q(AlwaysQ[4]));  // open: Reset, Qbar
  D_FlipFlop d_flipflop_6 (.D(multiplexer_14_out), .Clk(Clk), .Q(AlwaysQ[5]));  // open: Reset, Qbar
  D_FlipFlop d_flipflop_7 (.D(multiplexer_15_out), .Clk(Clk), .Q(AlwaysQ[6]));  // open: Reset, Qbar
  D_FlipFlop d_flipflop_8 (.D(multiplexer_16_out), .Clk(Clk), .Q(AlwaysQ[7]));  // open: Reset, Qbar
  assign Q = Enable ? AlwaysQ : 8'bz;  // Controlled_Buffer controlled_buffer_1
endmodule

module Negate8 (
  input  [7:0] A,
  output [7:0] NegA
);

  wire [7:0] not_1_out;

  // Probe on A
  not not_1 (not_1_out[0], A[0]);
  not not_2 (not_1_out[1], A[1]);
  not not_3 (not_1_out[2], A[2]);
  not not_4 (not_1_out[3], A[3]);
  not not_5 (not_1_out[4], A[4]);
  not not_6 (not_1_out[5], A[5]);
  not not_7 (not_1_out[6], A[6]);
  not not_8 (not_1_out[7], A[7]);
  CLA8 cla8_1 (.A(not_1_out), .B(8'h1), .Sum(NegA));  // open: Cin, C0
  // Probe on NegA
endmodule

module CLA8 (
  input  [7:0] A,
  input  [7:0] B,
  input  Cin,
  output C0,
  output [7:0] Sum
);

  wire cla4_1_gg, cla4_1_pg, cla4_2_gg, cla4_2_pg, lcu2_1_c1;

  // Probe on A
  // Probe on B
  CLA4 cla4_1 (.A(A[7:4]), .B(B[7:4]), .Cin(lcu2_1_c1), .Sum(Sum[7:4]), .PG(cla4_1_pg), .GG(cla4_1_gg));  // open: Cout
  CLA4 cla4_2 (.A(A[3:0]), .B(B[3:0]), .Cin(Cin), .Sum(Sum[3:0]), .PG(cla4_2_pg), .GG(cla4_2_gg));  // open: Cout
  LCU2 lcu2_1 (.P1(cla4_1_pg), .G1(cla4_1_gg), .P0(cla4_2_pg), .G0(cla4_2_gg), .C0(Cin), .C2(C0), .C1(lcu2_1_c1));
  // Probe on Sum
endmodule

module CLA4 (
  input  [3:0] A,
  input  [3:0] B,
  input  Cin,
  output Cout,
  output [3:0] Sum,
  output PG,
  output GG
);

  wire partialfulladder_1_g, partialfulladder_1_p, partialfulladder_2_g, partialfulladder_2_p,
       partialfulladder_3_g, partialfulladder_3_p, partialfulladder_4_g, partialfulladder_4_p;

  PartialFullAdder partialfulladder_1 (.A(A[3]), .B(B[3]), .P(partialfulladder_1_p), .G(partialfulladder_1_g));
  PartialFullAdder partialfulladder_2 (.A(A[2]), .B(B[2]), .P(partialfulladder_2_p), .G(partialfulladder_2_g));
  PartialFullAdder partialfulladder_3 (.A(A[1]), .B(B[1]), .P(partialfulladder_3_p), .G(partialfulladder_3_g));
  PartialFullAdder partialfulladder_4 (.A(A[0]), .B(B[0]), .P(partialfulladder_4_p), .G(partialfulladder_4_g));
  CLU4 clu4_1 (
    .P3(partialfulladder_1_p), .G3(partialfulladder_1_g), .P2(partialfulladder_2_p),
    .G2(partialfulladder_2_g), .P1(partialfulladder_3_p), .G1(partialfulladder_3_g),
    .P0(partialfulladder_4_p), .G0(partialfulladder_4_g), .C0(Cin), .PG(PG), .GG(GG), .C4(Cout), .S3(Sum[3]),
    .S2(Sum[2]), .S1(Sum[1]), .S0(Sum[0]));
  // Probe on Sum
endmodule

module PartialFullAdder (
  input  A,
  input  B,
  output P,
  output G
);

  and and_1 (G, A, B);
  xor xor_1 (P, A, B);
endmodule

module CLU4 (
  input  P3,
  input  G3,
  input  P2,
  input  G2,
  input  P1,
  input  G1,
  input  P0,
  input  G0,
  input  C0,
  output PG,
  output GG,
  output C4,
  output S3,
  output S2,
  output S1,
  output S0
);

  wire and_1_out, and_2_out, and_3_out, and_4_out, and_5_out, and_6_out, and_7_out, and_8_out, and_9_out,
       and_10_out, or_1_out, or_2_out, or_3_out;

  and and_1 (and_1_out, P3, P2, P1, P0, C0);
  and and_2 (and_2_out, P3, P2, P1, G0);
  and and_3 (and_3_out, P3, P2, G1);
  and and_4 (and_4_out, G2, P3);
  and and_5 (and_5_out, P2, P1, P0, C0);
  and and_6 (and_6_out, P2, P1, G0);
  and and_7 (and_7_out, G1, P2);
  and and_8 (and_8_out, P1, P0, C0);
  and and_9 (and_9_out, G0, P1);
  and and_10 (and_10_out, C0, P0);
  or or_1 (or_1_out, and_5_out, and_6_out, and_7_out, G2);
  or or_2 (or_2_out, and_8_out, and_9_out, G1);
  or or_3 (or_3_out, and_10_out, G0);
  and and_11 (PG, P3, P2, P1, P0);
  or or_4 (GG, and_2_out, and_3_out, and_4_out, G3);
  or or_5 (C4, and_1_out, and_2_out, and_3_out, and_4_out, G3);
  xor xor_1 (S3, P3, or_1_out);
  xor xor_2 (S2, P2, or_2_out);
  xor xor_3 (S1, P1, or_3_out);
  xor xor_4 (S0, P0, C0);
endmodule

module LCU2 (
  input  P1,
  input  G1,
  input  P0,
  input  G0,
  input  C0,
  output C2,
  output C1
);

  wire and_1_out, and_2_out, and_3_out;

  and and_1 (and_1_out, P1, P0, C0);
  and and_2 (and_2_out, G0, P1);
  and and_3 (and_3_out, C0, P0);
  or or_1 (C2, and_1_out, and_2_out, G1);
  or or_2 (C1, and_3_out, G0);
endmodule

module D_FlipFlop (
  input  D,
  input  Clk,
  input  Reset,
  output Q,
  output Qbar
);

  wire nand_1_out, nand_2_out, nand_3_out, nand_4_out, not_1_out;

  not not_1 (not_1_out, Reset);
  nand nand_1 (nand_1_out, nand_4_out, nand_2_out);
  nand nand_2 (nand_2_out, nand_1_out, Clk, not_1_out);
  nand nand_3 (nand_3_out, nand_2_out, Clk, nand_4_out);
  nand nand_4 (nand_4_out, nand_3_out, D, not_1_out);
  nand nand_5 (Q, nand_2_out, Qbar);
  nand nand_6 (Qbar, Q, nand_3_out, not_1_out);
endmodule

module D_Latch (
  input  D,
  input  Enable,
  output Q,
  output Qbar
);

  wire nand_1_out, nand_2_out, not_1_out;

  not not_1 (not_1_out, D);
  nand nand_1 (nand_1_out, D, Enable);
  nand nand_2 (nand_2_out, Enable, not_1_out);
  nand nand_3 (Q, nand_1_out, Qbar);
  nand nand_4 (Qbar, Q, nand_2_out);
endmodule

module BankSelect (
  input  [7:0] D,
  input  Load,
  input  Enable,
  input  Clk,
  input  Reset,
  output [7:0] Q,
  output [7:0] AlwaysQ
);

  wire multiplexer_1_out, multiplexer_2_out, multiplexer_3_out, multiplexer_4_out, multiplexer_5_out,
       multiplexer_6_out, multiplexer_7_out, multiplexer_8_out;
  wire [7:0] register8_1_alwaysq;

  Register8 register8_1 (.D(D), .Load(1'b1), .Clk(Clk), .AlwaysQ(register8_1_alwaysq));  // open: Enable, Reset, Q
  Multiplexer multiplexer_1 (.in0(AlwaysQ[0]), .in1(register8_1_alwaysq[0]), .out(multiplexer_1_out), .sel(Load));
  Multiplexer multiplexer_2 (.in0(AlwaysQ[1]), .in1(register8_1_alwaysq[1]), .out(multiplexer_2_out), .sel(Load));
  Multiplexer multiplexer_3 (.in0(AlwaysQ[2]), .in1(register8_1_alwaysq[2]), .out(multiplexer_3_out), .sel(Load));
  Multiplexer multiplexer_4 (.in0(AlwaysQ[3]), .in1(register8_1_alwaysq[3]), .out(multiplexer_4_out), .sel(Load));
  Multiplexer multiplexer_5 (.in0(AlwaysQ[4]), .in1(register8_1_alwaysq[4]), .out(multiplexer_5_out), .sel(Load));
  Multiplexer multiplexer_6 (.in0(AlwaysQ[5]), .in1(register8_1_alwaysq[5]), .out(multiplexer_6_out), .sel(Load));
  Multiplexer multiplexer_7 (.in0(AlwaysQ[6]), .in1(register8_1_alwaysq[6]), .out(multiplexer_7_out), .sel(Load));
  Multiplexer multiplexer_8 (.in0(AlwaysQ[7]), .in1(register8_1_alwaysq[7]), .out(multiplexer_8_out), .sel(Load));
  D_FlipFlop d_flipflop_1 (.D(multiplexer_1_out), .Clk(Clk), .Reset(Reset), .Q(AlwaysQ[0]));  // open: Qbar
  D_FlipFlop d_flipflop_2 (.D(multiplexer_2_out), .Clk(Clk), .Reset(Reset), .Q(AlwaysQ[1]));  // open: Qbar
  D_FlipFlop d_flipflop_3 (.D(multiplexer_3_out), .Clk(Clk), .Reset(Reset), .Q(AlwaysQ[2]));  // open: Qbar
  D_FlipFlop d_flipflop_4 (.D(multiplexer_4_out), .Clk(Clk), .Reset(Reset), .Q(AlwaysQ[3]));  // open: Qbar
  D_FlipFlop d_flipflop_5 (.D(multiplexer_5_out), .Clk(Clk), .Reset(Reset), .Q(AlwaysQ[4]));  // open: Qbar
  D_FlipFlop d_flipflop_6 (.D(multiplexer_6_out), .Clk(Clk), .Reset(Reset), .Q(AlwaysQ[5]));  // open: Qbar
  D_FlipFlop d_flipflop_7 (.D(multiplexer_7_out), .Clk(Clk), .Reset(Reset), .Q(AlwaysQ[6]));  // open: Qbar
  D_FlipFlop d_flipflop_8 (.D(multiplexer_8_out), .Clk(Clk), .Reset(Reset), .Q(AlwaysQ[7]));  // open: Qbar
  assign Q = Enable ? AlwaysQ : 8'bz;  // Controlled_Buffer controlled_buffer_1
endmodule
